# Fritzing sketch co326 (saved by Fritzing 0.9.10b)
breadboards: 1

parts:
  R1 = Resistor [tolerance=±5% resistance=10k power=0.25 package=THT]
  M1 = MAX30102
  DS1 = DS18B20 1-Wire Temperature Sensor Probe
  SW1 = Slide_Switch_new
  HLK-PM1 = HLK-PM01
  M3 = DOIT Esp32 DevKit v1 (30 pins long, 11 pins width) [part_number=ESP32S-PIN30]
  SIM800L_BO2 = SIM800L BO
  LED1 = smd LED [color="Red (633nm)" package="1206 [SMD]"]  # not connected
  J1 = Piezo Speaker  # not connected
  R2 = Resistor [tolerance=±5% resistance=10k power=0.25 package=THT]

nets:
  N1: R1.Pin_0, M3.D5
  N2: R1.Pin_1, DS1.DQ
  VIN: M1.VIN, DS1.VDD, M3.3V3, SIM800L_BO2.PIN1
  N3: M1.SCL, M3.D22
  N4: M1.INT, M3.D19
  GND: M1.GND, DS1.GND, HLK-PM1.-Vo, M3.GND, SIM800L_BO2.pin_5
  N5: SW1.pin_1, M3.VIN
  N6: SW1.pin_2, HLK-PM1.+Vo
  N7: M3.D2, SIM800L_BO2.PIN3
  N8: M3.D4, SIM800L_BO2.pin_4
  N9: M3.D35, R2.Pin_1

notes:
  SIM800L
  Temperature sensor (DS18B20)
  Pulse Sensor (MAX30100)
  Buzzer
  10kΩ
  1kΩ
  AC to DC power supply
  AC

custom parts:
  MAX30102: Oximeter module using the MAX30102 chip. You may wish to read (and check your module) this post on power problems with these modules: https://reedpaper.wordpress.com/2018/08/22/pulse-oximeter-max30100-max30102-how-to-fix-wrong-board/ . As usual, if you want the mounting holes in pcb, you need to drag a hole over the pad in silkscreen to actually drill the hole (by default they are not drilled)
  Slide_Switch_new: the New two pin slide switch
  DOIT Esp32 DevKit v1 (30 pins long, 11 pins width): The DOIT Esp32 DevKit v1 is one of the development board created by DOIT to evaluate the ESP-WROOM-32 module. It is based on the ESP32 microcontroller that boasts Wifi, Bluetooth, Ethernet and Low Power support all in a single chip. (vanepp) made breadboard work, adjusted pin numbering and labels and reduced size of schematic and cleaned up pcb. This chip is 30pins long (2 x15) and 11 pins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
